// Logisim project cpu.circ as structural Verilog
module \门电路测试  (
  input  in_1,
  input  in_2,
  input  in_3,
  input  in_4,
  input  in_5,
  input  in_6,
  input  in_7,
  input  in_8,
  input  in_9,
  input  in_10,
  input  in_11,
  input  in_12,
  input  in_13,
  input  in_14,
  input  in_15,
  input  in_16,
  input  in_17,
  input  in_18,
  input  in_19,
  input  in_20,
  input  in_21,
  input  in_22,
  input  in_23,
  input  in_24,
  input  in_25,
  input  in_26,
  input  in_27,
  input  in_28,
  input  in_29,
  input  in_30,
  input  in_31,
  input  in_32,
  input  in_33,
  input  in_34,
  input  in_35,
  input  in_36,
  input  in_37,
  input  in_38,
  input  in_39,
  input  in_40,
  input  in_41,
  input  in_42,
  input  in_43,
  input  in_44,
  input  in_45,
  input  in_46,
  input  in_47,
  input  in_48,
  input  in_49,
  input  in_50,
  input  in_51,
  input  in_52,
  output out_53,
  output out_54,
  output out_55,
  output out_56,
  output out_57,
  output out_58,
  output out_59,
  output out_60,
  output out_61,
  output out_62,
  output out_63,
  output out_64,
  output out_65,
  output out_66,
  output out_67,
  output out_68,
  output out_69,
  output out_70,
  output out_71,
  output out_72,
  output out_73,
  output out_74,
  output out_75,
  output out_76,
  output out_77,
  output out_78,
  output out_79,
  output out_80
);

  and and_1 (out_57, in_5, in_9);
  and and_2 (out_61, in_13, in_17);
  or or_1 (out_65, in_21, in_25);
  or or_2 (out_69, in_29, in_33);
  xor xor_1 (out_73, in_37, in_41);
  xor xor_2 (out_77, in_45, in_49);
  not not_1 (out_53, in_1);
  not not_2 (out_55, in_3);
  and and_3 (out_58, in_6, in_10);
  and and_4 (out_62, in_14, in_18);
  or or_3 (out_66, in_22, in_26);
  or or_4 (out_70, in_30, in_34);
  xor xor_3 (out_74, in_38, in_42);
  xor xor_4 (out_78, in_46, in_50);
  buf buffer_1 (out_54, in_2);
  buf buffer_2 (out_56, in_4);
  nand nand_1 (out_59, in_7, in_11);
  nand nand_2 (out_63, in_15, in_19);
  nor nor_1 (out_67, in_23, in_27);
  nor nor_2 (out_71, in_31, in_35);
  xnor xnor_1 (out_75, in_39, in_43);
  xnor xnor_2 (out_79, in_47, in_51);
  nand nand_3 (out_60, in_8, in_12);
  nand nand_4 (out_64, in_16, in_20);
  nor nor_3 (out_68, in_24, in_28);
  nor nor_4 (out_72, in_32, in_36);
  xnor xnor_3 (out_76, in_40, in_44);
  xnor xnor_4 (out_80, in_48, in_52);

  // Notes on the sheet:
  //   测试 非门
  //   测试 与门
  //   测试 或门
  //   测试 异或门
  //   测试 缓冲器
  //   测试 异或门
  //   测试 与非门
  //   测试 或非门
endmodule
